// Logisim project Digital Voting Machine Logisim.circ as structural Verilog: 1 circuit, main circuit main
module main (
  input  in_1,
  input  in_2,
  input  in_3
);

  wire and_1_out, and_2_out, and_3_out, n7447_1_pin3, n7447_1_pin5, n7447_1_pin9, n7447_1_pin10,
       n7447_1_pin11, n7447_1_pin12, n7447_1_pin13, n7447_1_pin14, n7447_1_pin15, n7447_2_pin3, n7447_2_pin5,
       n7447_2_pin9, n7447_2_pin10, n7447_2_pin11, n7447_2_pin12, n7447_2_pin13, n7447_2_pin14,
       n7447_2_pin15, n74163_1_pin1, n74163_1_pin7, n74163_1_pin10, n74163_1_pin11, n74163_1_pin12,
       n74163_1_pin13, n74163_1_pin14, n74163_2_pin1, n74163_2_pin7, n74163_2_pin10, n74163_2_pin11,
       n74163_2_pin12, n74163_2_pin13, n74163_2_pin14, not_1_out;

  not not_1 (not_1_out, in_1);
  and and_1 (and_1_out, in_1, in_3);
  and and_2 (and_2_out, in_2, not_1_out);
  _74163 u_74163_1 (
    .pin1(n74163_1_pin1), .pin2(and_1_out), .pin7(n74163_1_pin7), .pin14(n74163_1_pin14),
    .pin13(n74163_1_pin13), .pin12(n74163_1_pin12), .pin11(n74163_1_pin11), .pin10(n74163_1_pin10),
    .pin9(n74163_1_pin10));  // open: pin3, pin4, pin5, pin6, pin15
  and and_3 (and_3_out, and_2_out, in_3);
  _74163 u_74163_2 (
    .pin1(n74163_2_pin1), .pin2(and_3_out), .pin7(n74163_2_pin7), .pin14(n74163_2_pin14),
    .pin13(n74163_2_pin13), .pin12(n74163_2_pin12), .pin11(n74163_2_pin11), .pin10(n74163_2_pin10),
    .pin9(n74163_2_pin10));  // open: pin3, pin4, pin5, pin6, pin15
  _7447 u_7447_1 (
    .pin1(n74163_1_pin13), .pin2(n74163_1_pin12), .pin3(n7447_1_pin3), .pin5(n7447_1_pin5),
    .pin6(n74163_1_pin11), .pin7(n74163_1_pin14), .pin15(n7447_1_pin15), .pin14(n7447_1_pin14),
    .pin13(n7447_1_pin13), .pin12(n7447_1_pin12), .pin11(n7447_1_pin11), .pin10(n7447_1_pin10),
    .pin9(n7447_1_pin9));  // open: pin4
  _7_Segment_Display #(.active("false"), .decimalPoint("false")) u_7_segment_display_1 (
    .g(n7447_1_pin14), .f(n7447_1_pin15), .a(n7447_1_pin13), .b(n7447_1_pin12), .e(n7447_1_pin9),
    .d(n7447_1_pin10), .c(n7447_1_pin11));
  _7447 u_7447_2 (
    .pin1(n74163_2_pin13), .pin2(n74163_2_pin12), .pin3(n7447_2_pin3), .pin5(n7447_2_pin5),
    .pin6(n74163_2_pin11), .pin7(n74163_2_pin14), .pin15(n7447_2_pin15), .pin14(n7447_2_pin14),
    .pin13(n7447_2_pin13), .pin12(n7447_2_pin12), .pin11(n7447_2_pin11), .pin10(n7447_2_pin10),
    .pin9(n7447_2_pin9));  // open: pin4
  _7_Segment_Display #(.active("false"), .decimalPoint("false")) u_7_segment_display_2 (
    .g(n7447_2_pin14), .f(n7447_2_pin15), .a(n7447_2_pin13), .b(n7447_2_pin12), .e(n7447_2_pin9),
    .d(n7447_2_pin10), .c(n7447_2_pin11));
  // also tied to VCC on the sheet: {n74163_1_pin7, n74163_1_pin1, n74163_1_pin10, n74163_2_pin7, n7447_1_pin3, n7447_1_pin5, n74163_2_pin1, n74163_2_pin10, n7447_2_pin3, n7447_2_pin5}
endmodule
